// Logisim project 16bitMultiCycleMIPS.circ as structural Verilog: 7 circuits, main circuit main
module main (
  input  in_1,
  input  [15:0] forPC,
  output [5:0] out_3,
  output [15:0] out_4,
  output [15:0] out_5,
  output [1:0] AluMux2
);

  wire alu_1_zero, and_1_out, CLK, maincontroll_1_alumux1, maincontroll_1_out_6, maincontroll_1_out_7,
       maincontroll_1_out_8, maincontroll_1_out_9, maincontroll_1_out_11, maincontroll_1_out_15,
       maincontroll_1_pcwrite, maincontroll_1_regwrite, or_1_out;
  wire [1:0] maincontroll_1_pcmux;
  wire [3:0] maincontroll_1_out_16, multiplexer_2_out;
  wire [15:0] AluOut_q, DataReg2_q, DataReg_q, multiplexer_1_out, multiplexer_3_out, multiplexer_4_out,
       multiplexer_5_out, multiplexer_6_out, n16regfile_1_out_7, n16regfile_1_out_8, register_1_q;
  wire [25:16] IR_q;
  wire [31:0] bit_extender_1_out, DATA_q, inst_datamemory_1_out_5;

  or or_1 (or_1_out, and_1_out, maincontroll_1_pcwrite);
  Register #(.width(16)) register_1 (.D(multiplexer_6_out), .en(or_1_out), .Q(register_1_q), .clk(CLK), .clr(in_1));
  Multiplexer #(.width(16), .enable("false")) multiplexer_1 (
    .in0(register_1_q), .in1(AluOut_q), .out(multiplexer_1_out), .sel(maincontroll_1_out_6));
  Inst_DataMemory inst_datamemory_1 (
    .in_2(bit_extender_1_out), .in_3(multiplexer_1_out), .out_5(inst_datamemory_1_out_5),
    .WE(maincontroll_1_out_7), .CLK(CLK));
  Register #(.width(32)) IR (
    .D(inst_datamemory_1_out_5), .en(maincontroll_1_out_8), .Q({out_3, IR_q, out_5}), .clk(CLK));  // open: clr
  Register #(.width(32)) DATA (.D(inst_datamemory_1_out_5), .Q(DATA_q), .clk(CLK));  // open: en, clr
  Multiplexer #(.width(4), .enable("false")) multiplexer_2 (
    .in0(IR_q[19:16]), .in1(out_5[14:11]), .out(multiplexer_2_out), .sel(maincontroll_1_out_9));
  Multiplexer #(.width(16), .enable("false")) multiplexer_3 (
    .in0(AluOut_q), .in1(DATA_q[15:0]), .out(multiplexer_3_out), .sel(maincontroll_1_out_11));
  MainControll maincontroll_1 (
    .Funct(out_5[5:0]), .out_16(maincontroll_1_out_16), .PCWrite(maincontroll_1_pcwrite),
    .out_6(maincontroll_1_out_6), .out_7(maincontroll_1_out_7), .out_8(maincontroll_1_out_8),
    .out_9(maincontroll_1_out_9), .PCMux(maincontroll_1_pcmux), .out_11(maincontroll_1_out_11),
    .RegWrite(maincontroll_1_regwrite), .AluMux1(maincontroll_1_alumux1), .AluMux2(AluMux2),
    .out_15(maincontroll_1_out_15), .in_3(in_1), .in_1(CLK), .in_2(out_3));
  _16RegFile u_16regfile_1 (
    .A1(IR_q[24:21]), .A3(multiplexer_2_out), .A2(IR_q[19:16]), .WD3(multiplexer_3_out),
    .out_7(n16regfile_1_out_7), .out_8(n16regfile_1_out_8), .in_6(maincontroll_1_regwrite), .in_5(CLK));
  Clock clock_1 (.out(CLK));
  Register #(.width(16)) DataReg (.D(n16regfile_1_out_7), .Q(DataReg_q), .clk(CLK));  // open: en, clr
  Register #(.width(16)) DataReg2 (.D(n16regfile_1_out_8), .Q(DataReg2_q), .clk(CLK));  // open: en, clr
  Multiplexer #(.width(16), .enable("false")) multiplexer_4 (
    .in0(register_1_q), .in1(DataReg_q), .out(multiplexer_4_out), .sel(maincontroll_1_alumux1));
  Multiplexer #(.select(2), .width(16), .enable("false")) multiplexer_5 (
    .in0(out_5), .in1(DataReg2_q), .in3(forPC), .out(multiplexer_5_out), .sel(AluMux2));  // open: in2
  ALU alu_1 (
    .Data1(multiplexer_4_out), .Data2(multiplexer_5_out), .out_5(out_4), .Zero(alu_1_zero),
    .in_2(maincontroll_1_out_16), .Shamp(out_5[9:6]));
  assign bit_extender_1_out = {{16{1'b0}}, DataReg2_q};  // Bit_Extender bit_extender_1
  and and_1 (and_1_out, maincontroll_1_out_15, alu_1_zero);
  Register #(.width(16)) AluOut (.D(out_4), .Q(AluOut_q), .clk(CLK));  // open: en, clr
  Multiplexer #(.select(2), .width(16), .enable("false")) multiplexer_6 (
    .in0(out_4), .in1(AluOut_q), .in2(out_5), .out(multiplexer_6_out), .sel(maincontroll_1_pcmux));  // open: in3

  // Other names for the same wires on the sheet: IMM[15:0] = out_5; OP[5:0] = out_3; ALUOUT[15:0] = out_4

  // Notes on the sheet:
  //   PCWrite
  //   First before enabling clk, plese assert RST and deassert
  //   PCorALU
  //   DataWrite
  //   IRWrite
  //   Func
  //   shamp
  //   RegDst
  //   OP
  //   rs
  //   Imm
  //   DataToReg
  //   rt
  //   RegWrite
  //   AluMux1
  //   AluCont
  //   Branch
  //   PCMux
endmodule

module _16RegFile (
  input  [3:0] A1,
  input  [3:0] A3,
  input  [3:0] A2,
  input  [15:0] WD3,
  input  in_5,
  input  in_6,
  output [15:0] out_7,
  output [15:0] out_8
);

  wire and_1_out, and_2_out, and_3_out, and_4_out, and_5_out, and_6_out, and_7_out, and_8_out, and_9_out,
       and_10_out, and_11_out, and_12_out, and_13_out, and_14_out, and_15_out, and_16_out, decoder_1_out0,
       decoder_1_out1, decoder_1_out2, decoder_1_out3, decoder_1_out4, decoder_1_out5, decoder_1_out6,
       decoder_1_out7, decoder_1_out8, decoder_1_out9, decoder_1_out10, decoder_1_out11, decoder_1_out12,
       decoder_1_out13, decoder_1_out14, decoder_1_out15;
  wire [15:0] register_1_q, register_2_q, register_3_q, register_4_q, register_5_q, register_6_q,
       register_7_q, register_8_q, register_9_q, register_10_q, register_11_q, register_12_q, register_13_q,
       register_14_q, register_15_q, register_16_q;

  Decoder #(.select(4), .enable("false")) decoder_1 (
    .out0(decoder_1_out0), .out1(decoder_1_out1), .out2(decoder_1_out2), .out3(decoder_1_out3),
    .out4(decoder_1_out4), .out5(decoder_1_out5), .out6(decoder_1_out6), .out7(decoder_1_out7),
    .out8(decoder_1_out8), .out9(decoder_1_out9), .out10(decoder_1_out10), .out11(decoder_1_out11),
    .out12(decoder_1_out12), .out13(decoder_1_out13), .out14(decoder_1_out14), .out15(decoder_1_out15),
    .sel(A3));
  and and_1 (and_1_out, decoder_1_out0, in_6);
  and and_2 (and_2_out, decoder_1_out1, in_6);
  and and_3 (and_3_out, decoder_1_out2, in_6);
  and and_4 (and_4_out, decoder_1_out3, in_6);
  and and_5 (and_5_out, decoder_1_out4, in_6);
  and and_6 (and_6_out, decoder_1_out5, in_6);
  and and_7 (and_7_out, decoder_1_out6, in_6);
  and and_8 (and_8_out, decoder_1_out7, in_6);
  Register #(.width(16)) register_1 (.D(WD3), .en(and_1_out), .Q(register_1_q), .clk(in_5));  // open: clr
  Register #(.width(16)) register_2 (.D(WD3), .en(and_2_out), .Q(register_2_q), .clk(in_5));  // open: clr
  Register #(.width(16)) register_3 (.D(WD3), .en(and_3_out), .Q(register_3_q), .clk(in_5));  // open: clr
  Register #(.width(16)) register_4 (.D(WD3), .en(and_4_out), .Q(register_4_q), .clk(in_5));  // open: clr
  Register #(.width(16)) register_5 (.D(WD3), .en(and_5_out), .Q(register_5_q), .clk(in_5));  // open: clr
  Register #(.width(16)) register_6 (.D(WD3), .en(and_6_out), .Q(register_6_q), .clk(in_5));  // open: clr
  Register #(.width(16)) register_7 (.D(WD3), .en(and_7_out), .Q(register_7_q), .clk(in_5));  // open: clr
  Register #(.width(16)) register_8 (.D(WD3), .en(and_8_out), .Q(register_8_q), .clk(in_5));  // open: clr
  and and_9 (and_9_out, decoder_1_out8, in_6);
  and and_10 (and_10_out, decoder_1_out9, in_6);
  and and_11 (and_11_out, decoder_1_out10, in_6);
  and and_12 (and_12_out, decoder_1_out11, in_6);
  and and_13 (and_13_out, decoder_1_out12, in_6);
  and and_14 (and_14_out, decoder_1_out13, in_6);
  and and_15 (and_15_out, decoder_1_out14, in_6);
  and and_16 (and_16_out, decoder_1_out15, in_6);
  Register #(.width(16)) register_9 (.D(WD3), .en(and_9_out), .Q(register_9_q), .clk(in_5));  // open: clr
  Register #(.width(16)) register_10 (.D(WD3), .en(and_10_out), .Q(register_10_q), .clk(in_5));  // open: clr
  Register #(.width(16)) register_11 (.D(WD3), .en(and_11_out), .Q(register_11_q), .clk(in_5));  // open: clr
  Register #(.width(16)) register_12 (.D(WD3), .en(and_12_out), .Q(register_12_q), .clk(in_5));  // open: clr
  Register #(.width(16)) register_13 (.D(WD3), .en(and_13_out), .Q(register_13_q), .clk(in_5));  // open: clr
  Register #(.width(16)) register_14 (.D(WD3), .en(and_14_out), .Q(register_14_q), .clk(in_5));  // open: clr
  Register #(.width(16)) register_15 (.D(WD3), .en(and_15_out), .Q(register_15_q), .clk(in_5));  // open: clr
  Register #(.width(16)) register_16 (.D(WD3), .en(and_16_out), .Q(register_16_q), .clk(in_5));  // open: clr
  Multiplexer #(.select(4), .width(16), .enable("false")) multiplexer_1 (
    .in0(register_1_q), .in1(register_2_q), .in2(register_3_q), .in3(register_4_q), .in4(register_5_q),
    .in5(register_6_q), .in6(register_7_q), .in7(register_8_q), .in8(register_9_q), .in9(register_10_q),
    .in10(register_11_q), .in11(register_12_q), .in12(register_13_q), .in13(register_14_q),
    .in14(register_15_q), .in15(register_16_q), .out(out_7), .sel(A1));
  Multiplexer #(.select(4), .width(16), .enable("false")) multiplexer_2 (
    .in0(register_1_q), .in1(register_2_q), .in2(register_3_q), .in3(register_4_q), .in4(register_5_q),
    .in5(register_6_q), .in6(register_7_q), .in7(register_8_q), .in8(register_9_q), .in9(register_10_q),
    .in10(register_11_q), .in11(register_12_q), .in12(register_13_q), .in13(register_14_q),
    .in14(register_15_q), .in15(register_16_q), .out(out_8), .sel(A2));

  // Other names for the same wires on the sheet: clk = in_5; RegWrite = in_6
endmodule

module ALU (
  input  [15:0] Data1,
  input  [3:0] in_2,
  input  [15:0] Data2,
  input  [3:0] Shamp,
  output [15:0] out_5,
  output Zero
);

  wire comparator_1_lt;
  wire [15:0] adder_1_out, and_1_out, bit_extender_1_out, or_1_out, shifter_1_out, shifter_2_out,
       subtractor_1_out;

  Shifter #(.width(16)) shifter_1 (.in(Data2), .\dist (Shamp), .out(shifter_1_out));
  Shifter #(.width(16), .shift("lr")) shifter_2 (.in(Data2), .\dist (Shamp), .out(shifter_2_out));
  Adder #(.width(16)) adder_1 (.a(Data1), .b(Data2), .out(adder_1_out));  // open: cin, cout
  Subtractor #(.width(16)) subtractor_1 (.a(Data1), .b(Data2), .out(subtractor_1_out));  // open: bin, bout
  assign or_1_out = Data1 | Data2;  // OR_Gate or_1, 16 bits wide
  assign and_1_out = Data1 & Data2;  // AND_Gate and_1, 16 bits wide
  Comparator #(.width(16)) comparator_1 (.a(Data1), .b(Data2), .eq(Zero), .lt(comparator_1_lt));  // open: gt
  assign bit_extender_1_out = {{15{1'b0}}, comparator_1_lt};  // Bit_Extender bit_extender_1
  Multiplexer #(.select(4), .width(16), .enable("false")) multiplexer_1 (
    .in0(and_1_out), .in1(or_1_out), .in2(adder_1_out), .in6(subtractor_1_out), .in7(bit_extender_1_out),
    .in8(shifter_1_out), .in9(shifter_2_out), .out(out_5), .sel(in_2));  // open: in3, in4, in5, in10, in11, in12, in13, in14, in15
endmodule

module Inst_DataMemory (
  input  WE,
  input  [31:0] in_2,
  input  [15:0] in_3,
  input  CLK,
  output [31:0] out_5
);

  wire not_1_out;

  not not_1 (not_1_out, WE);
  assign out_5 = WE ? in_2 : 32'bz;  // Controlled_Buffer controlled_buffer_1
  RAM #(.addrWidth(16), .dataWidth(32)) ram_1 (.addr(in_3), .data(out_5), .clk(CLK), .ld(not_1_out));  // open: sel, clr

  // Notes on the sheet:
  //   WriteData
  //   Address
  //   we are using 32 bit Instruction. However data is 16 bit >= [31:16] = 0, so use it that way
  //   So as anyone can see, we are using RAM, so you have to save insruction again and again after quitting logisim
endmodule

module RingCounter (
  input  in_1,
  input  in_2,
  output [4:0] out_3
);

  D_Flip_Flop d_ff_1 (.clk(in_1), .D(out_3[4]), .Q(out_3[0]), .preset(in_2));  // open: Qn, en, reset
  D_Flip_Flop d_ff_2 (.clk(in_1), .D(out_3[0]), .Q(out_3[1]), .reset(in_2));  // open: Qn, preset, en
  D_Flip_Flop d_ff_3 (.clk(in_1), .D(out_3[1]), .Q(out_3[2]), .reset(in_2));  // open: Qn, preset, en
  D_Flip_Flop d_ff_4 (.clk(in_1), .D(out_3[2]), .Q(out_3[3]), .reset(in_2));  // open: Qn, preset, en
  D_Flip_Flop d_ff_5 (.clk(in_1), .D(out_3[3]), .Q(out_3[4]), .reset(in_2));  // open: Qn, preset, en
endmodule

module MainControll (
  input  in_1,
  input  [5:0] in_2,
  input  in_3,
  input  [5:0] Funct,
  output PCWrite,
  output out_6,
  output out_7,
  output out_8,
  output out_9,
  output [1:0] PCMux,
  output out_11,
  output RegWrite,
  output AluMux1,
  output [1:0] AluMux2,
  output out_15,
  output [3:0] out_16
);

  wire addf_out, and_1_out, and_2_out, and_3_out, and_4_out, and_5_out, and_6_out, and_7_out, and_8_out,
       and_9_out, and_10_out, andf_out, not_3_out, or_1_out, or_2_out, or_3_out, orf_out, sltf_out, subf_out;
  wire [1:0] not_2_out;
  wire [2:0] test_1_aluop;
  wire [5:0] not_1_out;

  assign not_1_out = ~Funct;  // NOT_Gate not_1, 6 bits wide
  assign not_2_out = ~test_1_aluop[1:0];  // NOT_Gate not_2, 2 bits wide
  not not_3 (not_3_out, test_1_aluop[2]);
  Test test_1 (
    .CLK(in_1), .in_3(in_3), .ALUop(test_1_aluop), .OPcode(in_2), .out_4(PCWrite), .out_5(out_6),
    .out_6(out_7), .out_7(out_8), .out_8(out_9), .out_10(out_11), .RegWrite(RegWrite), .AluMux1(AluMux1),
    .AluMux2(AluMux2), .out_14(out_15), .PCMux(PCMux));
  and and_1 (and_1_out, not_2_out[0], test_1_aluop[1]);
  and and_2 (and_2_out, not_2_out[0], not_2_out[1], not_3_out);
  and addf (addf_out, not_1_out[0], not_1_out[1], not_1_out[2], not_1_out[3], Funct[5]);
  and subf (subf_out, not_1_out[3], not_1_out[2], Funct[1], not_1_out[0]);
  and andf (andf_out, not_1_out[0], not_1_out[1], not_1_out[3], Funct[2]);
  and orf (orf_out, Funct[0], not_1_out[1], Funct[2], not_1_out[3]);
  and sltf (sltf_out, not_1_out[2], Funct[1], not_1_out[0], Funct[3]);
  and and_3 (and_3_out, and_1_out, addf_out);
  and and_4 (and_4_out, and_1_out, subf_out);
  and and_5 (and_5_out, and_1_out, andf_out);
  and and_6 (and_6_out, and_1_out, orf_out);
  and and_7 (and_7_out, and_1_out, sltf_out);
  and and_8 (and_8_out, not_1_out[4], and_1_out, not_1_out[5], not_1_out[3], not_1_out[2], not_1_out[1], not_1_out[0]);
  and and_9 (and_9_out, and_1_out, not_1_out[4], not_1_out[5], not_1_out[3], not_1_out[2], not_1_out[1], Funct[0]);
  or or_1 (or_1_out, and_3_out, and_2_out);
  and and_10 (and_10_out, not_2_out[1], test_1_aluop[0]);
  or or_2 (or_2_out, and_10_out, and_4_out);
  or or_3 (or_3_out, and_6_out, test_1_aluop[2]);
  or or_4 (out_16[2], or_2_out, and_7_out);
  or or_5 (out_16[3], and_8_out, and_9_out);
  or or_6 (out_16[1], or_1_out, out_16[2]);
  or or_7 (out_16[0], or_3_out, and_9_out, and_7_out);

  // Notes on the sheet:
  //   PCorALU
  //   DataWrite
  //   IRWrite
  //   RegDst
  //   DataToReg
  //   add
  //   sub
  //   and
  //   or
  //   slt
  //   sll
  //   srl
  //   Branch
endmodule

module Test (
  input  [5:0] OPcode,
  input  CLK,
  input  in_3,
  output out_4,
  output out_5,
  output out_6,
  output out_7,
  output out_8,
  output [1:0] PCMux,
  output out_10,
  output RegWrite,
  output AluMux1,
  output [1:0] AluMux2,
  output out_14,
  output [2:0] ALUop
);

  wire not_1_out, or_1_out;
  wire [3:0] counter_1_q, multiplexer_1_out, rom_1_data;
  wire [4:0] ringcounter_1_out_3;

  RingCounter ringcounter_1 (.in_1(CLK), .in_2(in_3), .out_3(ringcounter_1_out_3));
  ROM #(.addrWidth(6), .dataWidth(4)) rom_1 (.addr(OPcode), .data(rom_1_data));  // open: sel
  or or_1 (or_1_out, ringcounter_1_out_3[0], ringcounter_1_out_3[2]);
  Multiplexer #(.width(4), .enable("false")) multiplexer_1 (
    .in0(rom_1_data), .in1(4'b0000), .out(multiplexer_1_out), .sel(ringcounter_1_out_3[0]));
  not not_1 (not_1_out, or_1_out);
  Counter #(.width(4), .max('hf)) counter_1 (
    .load(or_1_out), .D(multiplexer_1_out), .count(not_1_out), .Q(counter_1_q), .clk(CLK));  // open: carry, clr
  ROM #(.addrWidth(4), .dataWidth(16)) rom_2 (
    .addr(counter_1_q),
    .data({out_4, out_5, out_6, out_7, out_8, out_10, RegWrite, AluMux1, AluMux2, out_14, PCMux, ALUop}));  // open: sel

  // Notes on the sheet:
  //   PCWrite
  //   Some kind of microprogramming, i guess
  //   PCorALU
  //   DataWrite
  //   contents of rom_1 (hex, n*v repeats v):
  //   2 a a 0 9 0 0 0 9 7*0 b 18*0 4 7*0 7
  //   IRWrite
  //   RegDst
  //   DataToReg
  //   contents of rom_2 (hex, n*v repeats v):
  //   90c0 0 142 a00 100 4000 600 100 6000 169 8010 100 200
  //   max 5 states
  //   S0 = fetch(at address 0000)
  //   S1 = decode(at address 0001)
  //   the other states outputs depend on OPCode)
  //   R-type inst address: 0010
  //   lw-address: 0100
  //   sw-address 0111
  //   beq-address 1001
  //   j-address: 1010
  //   addi-address: 1011
  //   Branch
endmodule
